# Fritzing sketch Untitled Sketch 2 (saved by Fritzing 0.9.3b)

parts:
  R1_5K = Resistor [tolerance=±5% resistance=220 package=THT]
  R2_10K = Resistor [tolerance=±5% resistance=220 package=THT]
  Mod1 = ESP32 - CAM
  S1 = Pushbutton [package="[THT]"]
  R3_47 = Resistor [tolerance=±5% resistance=220 package=THT]
  LED1 = LED - 3mm [color="Red (633nm)" package="3 mm [THT]"]
  5V = Power plug

nets:
  N1: R1_5K.Pin_0, S1.Pin_3, S1.Pin_4
  N2: R1_5K.Pin_1, Mod1.IO13
  N3: R2_10K.Pin_0, Mod1.3V3, S1.Pin_1, S1.Pin_2
  GND: R2_10K.Pin_1, Mod1.GND, LED1.cathode, 5V.GND
  5V: Mod1.5V, 5V.VCC
  N4: Mod1.IO14, R3_47.Pin_1

custom parts:
  ESP32 - CAM: The ESP32-CAM has a very competitive small-size camera module that can operate independently as a minimum system with a footprint of only 27*40.5*4.5mm and a deep sleep current of up to 6mA.
